# Fritzing sketch abat-jour_automatique (saved by Fritzing 0.9.3b)
circuit board: 8.46667cm x 5.64444cm
breadboards: 1

parts:
  Placa_Arduino_Uno_R3 = Arduino Uno (Rev3)
  Módulo_Bluetooth_HC-05 = Bluetooth HC-05 Macho
  Relay = Keyes Relay [package=THT]
  R2 = Resistor [tolerance=±5% resistance=2.2k package=THT]
  R3 = Resistor [tolerance=±5% resistance=1k package=THT]

nets:
  N1: Placa_Arduino_Uno_R3.D8, Relay.signal
  N2: Placa_Arduino_Uno_R3.D0/RX, Módulo_Bluetooth_HC-05.TXD
  N3: Placa_Arduino_Uno_R3.D1/TX, R3.Pin_0
  5V: Placa_Arduino_Uno_R3.5V, Módulo_Bluetooth_HC-05.VCC, Relay.power
  GND: Placa_Arduino_Uno_R3.GND, Módulo_Bluetooth_HC-05.GND, Relay.ground, R2.Pin_1
  N4: Módulo_Bluetooth_HC-05.RXD, R2.Pin_0, R3.Pin_1

custom parts:
  Keyes Relay: The Keyes 5V relay module is suitable for SCM development, home appliance control. It uses a 5V~12V TIL control signal which can control DC / AC signal.

// code stored in the sketch: abat-jour_automatique.ino

